# Fritzing sketch Radio Frequencia com Adaptador (saved by Fritzing 0.9.10b)

parts:
  Componente1 = Arduino Uno (Rev3) - ICSP
  M1 = NRF24L01-BO [package=THT]

nets:
  N1: Componente1.D8, M1.CSN
  N2: Componente1.D11_PWM/MOSI, M1.M0
  N3: Componente1.D12/MISO, M1.M1
  N4: Componente1.D13/SCK, M1.SCK
  N5: Componente1.D7, M1.CE
  5V: Componente1.5V, M1.VCC
  GND: Componente1.GND, M1.GND

custom parts:
  NRF24L01-BO: NRF24L01-BO breakout board for the NRF24L01. Pcb view suppressed as unneeded.
