# Fritzing sketch Radio Frequencia (saved by Fritzing 0.9.10b)
breadboards: 1

parts:
  Componente1 = NRF24L01+ Breakout Board
  Componente2 = Arduino Uno (Rev3) - ICSP

nets:
  GND: Componente1.GND, Componente2.GND
  VCC: Componente1.VCC, Componente2.3V3
  N1: Componente1.CE, Componente2.D9_PWM
  N2: Componente1.CS, Componente2.D10_PWM/SS
  N3: Componente1.SCK, Componente2.D13/SCK
  N4: Componente1.MOSI, Componente2.ICSP_MOSI, Componente2.D11_PWM/MOSI
  N5: Componente1.MISO, Componente2.D12/MISO
